// Logisim project ComparatorCircuit.circ as structural Verilog: 5 circuits, main circuit 7-bit FA
module _7_bit_FA (
  input  Cin,
  input  A0,
  input  B0,
  input  A1,
  input  B1,
  input  A2,
  input  B2,
  input  A3,
  input  B3,
  input  A4,
  input  B4,
  input  A5,
  input  B5,
  input  A6,
  input  B6,
  output S0,
  output S1,
  output S2,
  output S3,
  output S4,
  output S5,
  output S6,
  output Cout
);

  wire full_adder_1_cout, full_adder_2_cout, full_adder_3_cout, full_adder_4_cout, full_adder_5_cout,
       full_adder_6_cout;

  full_adder full_adder_1 (.A(A0), .B(B0), .Cin(Cin), .S(S0), .Cout(full_adder_1_cout));
  full_adder full_adder_2 (.A(A1), .B(B1), .Cin(full_adder_1_cout), .S(S1), .Cout(full_adder_2_cout));
  full_adder full_adder_3 (.A(A2), .B(B2), .Cin(full_adder_2_cout), .S(S2), .Cout(full_adder_3_cout));
  full_adder full_adder_4 (.A(A3), .B(B3), .Cin(full_adder_3_cout), .S(S3), .Cout(full_adder_4_cout));
  full_adder full_adder_5 (.A(A4), .B(B4), .Cin(full_adder_4_cout), .S(S4), .Cout(full_adder_5_cout));
  full_adder full_adder_6 (.A(A5), .B(B5), .Cin(full_adder_5_cout), .S(S5), .Cout(full_adder_6_cout));
  full_adder full_adder_7 (.A(A6), .B(B6), .Cin(full_adder_6_cout), .S(S6), .Cout(Cout));
endmodule

// FA
module full_adder (
  input  A,
  input  B,
  input  Cin,
  output S,
  output Cout
);

  wire and_1_out, and_2_out, xor_1_out;

  xor xor_1 (xor_1_out, A, B);
  xor xor_2 (S, xor_1_out, Cin);
  and and_1 (and_1_out, xor_1_out, Cin);
  and and_2 (and_2_out, A, B);
  or or_1 (Cout, and_1_out, and_2_out);
endmodule

module Comparator (
  input  A6,
  input  A5,
  input  A4,
  input  A3,
  input  A2,
  input  A1,
  input  A0,
  input  Cin,
  input  B0,
  input  B1,
  input  B2,
  input  B3,
  input  B4,
  input  B5,
  input  B6,
  output A__B,
  output A__B_2,
  output A__B_3,
  output A__B____Q
);

  wire n7_bit_fa_1_s0, n7_bit_fa_1_s1, n7_bit_fa_1_s2, n7_bit_fa_1_s3, n7_bit_fa_1_s4, n7_bit_fa_1_s5,
       n7_bit_fa_1_s6, not_1_out, not_2_out, not_3_out, not_4_out, not_5_out, not_6_out, not_7_out;

  not not_1 (not_1_out, A0);
  not not_2 (not_2_out, A1);
  not not_3 (not_3_out, A2);
  not not_4 (not_4_out, A3);
  not not_5 (not_5_out, A4);
  not not_6 (not_6_out, A5);
  not not_7 (not_7_out, A6);
  _7_bit_FA u_7_bit_fa_1 (
    .A0(not_1_out), .B0(B0), .A1(not_2_out), .B1(B1), .A2(not_3_out), .B2(B2), .A3(not_4_out), .B3(B3),
    .A4(not_5_out), .B4(B4), .A5(not_6_out), .B5(B5), .A6(not_7_out), .B6(B6), .Cin(Cin),
    .S0(n7_bit_fa_1_s0), .S1(n7_bit_fa_1_s1), .S2(n7_bit_fa_1_s2), .S3(n7_bit_fa_1_s3), .S4(n7_bit_fa_1_s4),
    .S5(n7_bit_fa_1_s5), .S6(n7_bit_fa_1_s6), .Cout(A__B____Q));
  and and_1 (A__B, n7_bit_fa_1_s0, n7_bit_fa_1_s1, n7_bit_fa_1_s2, n7_bit_fa_1_s3, n7_bit_fa_1_s4, n7_bit_fa_1_s5, n7_bit_fa_1_s6);
  or or_1 (A__B_2, A__B, ~A__B____Q);  // OR_Gate
  or or_2 (A__B_3, A__B, A__B____Q);
endmodule

module Mux (
  input  A,
  input  S,
  input  B,
  output out_4
);

  wire and_1_out, and_2_out, not_1_out;

  not not_1 (not_1_out, S);
  and and_1 (and_1_out, A, S);
  and and_2 (and_2_out, not_1_out, B);
  or or_1 (out_4, and_1_out, and_2_out);
endmodule

module Full_design (
  input  load,
  input  Enable,
  input  [6:0] M,
  input  in_4,
  input  count,
  input  RESET,
  input  in_7,
  input  in_8,
  input  in_9,
  input  in_10,
  input  in_11,
  input  in_12,
  input  in_13,
  output [6:0] C,
  output Z__Q_0,
  output Y__C____M,
  output X___C____M,
  output W____Q,
  output CO
);

  wire and_1_out, and_2_out, and_3_out, and_5_out, and_6_out, and_7_out, and_8_out, CLK_out, mux_1_out_4,
       mux_2_out_4, mux_3_out_4, mux_4_out_4, mux_5_out_4, mux_6_out_4, mux_7_out_4, not_1_out, xor_1_out,
       xor_2_out, xor_3_out, xor_4_out, xor_5_out, xor_6_out, xor_7_out;

  not not_1 (not_1_out, load);
  and and_1 (and_1_out, not_1_out, count);
  and and_2 (and_2_out, and_1_out, C[0]);
  and and_3 (and_3_out, and_2_out, C[1]);
  and and_4 (CO, and_8_out, C[6]);
  and and_5 (and_5_out, and_3_out, C[2]);
  and and_6 (and_6_out, and_5_out, C[3]);
  and and_7 (and_7_out, and_6_out, C[4]);
  and and_8 (and_8_out, and_7_out, C[5]);
  xor xor_1 (xor_1_out, and_1_out, C[0]);
  xor xor_2 (xor_2_out, and_2_out, C[1]);
  xor xor_3 (xor_3_out, and_3_out, C[2]);
  xor xor_4 (xor_4_out, and_5_out, C[3]);
  xor xor_5 (xor_5_out, and_6_out, C[4]);
  xor xor_6 (xor_6_out, and_7_out, C[5]);
  xor xor_7 (xor_7_out, and_8_out, C[6]);
  Mux mux_1 (.A(in_4), .S(load), .B(xor_1_out), .out_4(mux_1_out_4));
  Mux mux_2 (.A(in_7), .S(load), .B(xor_2_out), .out_4(mux_2_out_4));
  Mux mux_3 (.A(in_8), .S(load), .B(xor_3_out), .out_4(mux_3_out_4));
  Mux mux_4 (.A(in_10), .S(load), .B(xor_4_out), .out_4(mux_4_out_4));
  Mux mux_5 (.A(in_11), .S(load), .B(xor_5_out), .out_4(mux_5_out_4));
  Mux mux_6 (.A(in_12), .S(load), .B(xor_6_out), .out_4(mux_6_out_4));
  Mux mux_7 (.A(in_13), .S(load), .B(xor_7_out), .out_4(mux_7_out_4));
  D_Flip_Flop d_ff_1 (.clk(CLK_out), .D(mux_1_out_4), .Q(C[0]), .en(Enable), .reset(RESET));  // open: Qn, preset
  D_Flip_Flop d_ff_2 (.clk(CLK_out), .D(mux_2_out_4), .Q(C[1]), .en(Enable), .reset(RESET));  // open: Qn, preset
  D_Flip_Flop d_ff_3 (.clk(CLK_out), .D(mux_3_out_4), .Q(C[2]), .en(Enable), .reset(RESET));  // open: Qn, preset
  D_Flip_Flop d_ff_4 (.clk(CLK_out), .D(mux_4_out_4), .Q(C[3]), .en(Enable), .reset(RESET));  // open: Qn, preset
  D_Flip_Flop d_ff_5 (.clk(CLK_out), .D(mux_5_out_4), .Q(C[4]), .en(Enable), .reset(RESET));  // open: Qn, preset
  D_Flip_Flop d_ff_6 (.clk(CLK_out), .D(mux_6_out_4), .Q(C[5]), .en(Enable), .reset(RESET));  // open: Qn, preset
  D_Flip_Flop d_ff_7 (.clk(CLK_out), .D(mux_7_out_4), .Q(C[6]), .en(Enable), .reset(RESET));  // open: Qn, preset
  Clock CLK (.out(CLK_out));
  Comparator comparator_1 (
    .B0(M[0]), .B1(M[1]), .B2(M[2]), .B3(M[3]), .B4(M[4]), .B5(M[5]), .B6(M[6]), .A6(C[6]), .A5(C[5]),
    .A4(C[4]), .A3(C[3]), .A2(C[2]), .A1(C[1]), .A0(C[0]), .Cin(in_9), .A__B(Z__Q_0), .A__B_2(Y__C____M),
    .A__B_3(X___C____M), .A__B____Q(W____Q));
endmodule
